# Fritzing sketch Schematic (saved by Fritzing 0.9.3b)
perfboards: 1

parts:
  L298N1 = L298N DC motor driver
  Componente1 = Arduino Uno (Rev3)
  hc-sr1 = hc-sr04
  LED1 = LED - 3mm [color="Red (633nm)" package="3 mm [THT]"]
  LED2 = LED - 3mm [color="Red (633nm)" package="3 mm [THT]"]
  S2 = Pushbutton [package="[THT]"]
  VCC1 = Battery block 9V
  U1 = SWITCH_SPDT [package=kps-1290]
  R1 = Resistor [tolerance=±5% resistance=470 package="0402 [SMD]"]
  R2 = Resistor [tolerance=±5% resistance=470 package="0402 [SMD]"]
  R3 = Resistor [tolerance=±5% resistance=1k package="0402 [SMD]"]

nets:
  12V: L298N1.12V, Componente1.VIN, U1.P
  GND: L298N1.GND, Componente1.GND, hc-sr1.GND, VCC1.-, R1.Pin_1, R2.Pin_1, R3.Pin_1
  N1: L298N1.5V, Componente1.D9_PWM, S2.Pin_3, S2.Pin_4, R3.Pin_0
  N2: L298N1.ENA, Componente1.D10_PWM/SS
  N3: L298N1.ENB, Componente1.D11_PWM/MOSI
  N4: L298N1.IN1, Componente1.D4
  N5: L298N1.IN2, Componente1.D5_PWM
  N6: L298N1.IN3, Componente1.D6_PWM
  N7: L298N1.IN4, Componente1.D7
  N8: Componente1.D12/MISO, LED1.anode
  N9: Componente1.D13/SCK, LED2.anode
  N10: Componente1.D2, hc-sr1.Trig
  N11: Componente1.D3_PWM, hc-sr1.Echo
  5V: Componente1.5V, hc-sr1.VCC
  N12: LED1.cathode, R1.Pin_0
  N13: LED2.cathode, R2.Pin_0
  N14: S2.Pin_1, S2.Pin_2
  N15: VCC1.+, U1.O

custom parts:
  L298N DC motor driver: 2x DC motor driver with 78M05 positive voltage regulator (7..35 V) L298N: max 46 V, 2 A Set 5 V Enable jumper to enable 5 V regultor (needed for the L298N) and +5 V output at screw terminal or supply external +5 V at screw terminal Set ENA and/or ENB to +5 V to enable motor permanently or supply ENA and/or ENB with PWM signal IN1 and IN2 set rotation directory for motor A (OUT1/OUT2) IN2 and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
